# Fritzing sketch Arduino Uno Rev3 - DHT22 Schematic (saved by Fritzing 0.9.3b)
breadboards: 1

parts:
  Εξάρτημα1 = Arduino Uno (Rev3) - ICSP
  RHT1 = Humidity and Temperature Sensor RHT03

nets:
  N1: Εξάρτημα1.D2, RHT1.Data-signal
  5V: Εξάρτημα1.5V, RHT1.Vcc
  N2: Εξάρτημα1.GND, RHT1.GND_2
