# Fritzing sketch Arduino Uno Rev3 - Arduino Ethernet Shield - DHT22 Electrological Schematic (saved by Fritzing 0.9.3b)
breadboards: 1

parts:
  Arduino_Uno_Rev3 = Arduino Uno (Rev3) - ICSP  # not connected
  Arduino_Ethernet_Shield = Arduino Ethernet Shield (Rev3)
  DHT22 = DHT22 Humidity and Temperature Sensor

nets:
  5V: Arduino_Ethernet_Shield.5V, DHT22.VDD
  GND: Arduino_Ethernet_Shield.GND, DHT22.GND
  N1: Arduino_Ethernet_Shield.D2, DHT22.DATA
