# Fritzing sketch WeMos D1 R2 - DHT22 Schematic (saved by Fritzing 0.9.3b)
breadboards: 1

parts:
  WeMos_D1_R1 = WeMos D1 R2
  RHT1 = Humidity and Temperature Sensor RHT03

nets:
  N1: WeMos_D1_R1.D2, RHT1.Data-signal
  N2: WeMos_D1_R1.GND, RHT1.GND_2
  5V: WeMos_D1_R1.5V, RHT1.Vcc

custom parts:
  WeMos D1 R2: The D1 R2 is a mini wifi board based on the ESP-8266EX.
